# Fritzing sketch led-base (saved by Fritzing 0.9.3b)
breadboards: 1

parts:
  Raspberry_Pi_1 = Raspberry Pi 3 [part_number=RPI-3-V1.2]
  LED1 = LED - 5mm [color="Red (633nm)" package="5 mm [THT]"]  # not connected
  R1 = Resistor [tolerance=±5% resistance=220 package="0603 [SMD]"]

nets:
  N1: Raspberry_Pi_1.GND, R1.Pin_1

notes:
  Rasberry PI 3
  Tarefa:
  Monte o circuito para conectar um LED ao Raspberry PI.
  Você pode procurar pelos componentes LED e resistor na paleta de componentes.
  No Raspberry PI use o PIN7 e PIN 25 (GND) para ligar o LED no Protoboard.
  Coloque a perna positiva do LED para lado esquerdo, perna negativa para lado direito.
  Lembre-se que o LED precisa de um resistor.
  Mãos à obra!

// code stored in the sketch: helloword.ino
gpio mode 7 out
gpio write 7 1
